// Logisim project 12BIT DATAPATH.circ as structural Verilog: 4 circuits, main circuit Datapath
module Datapath (
  input  [11:0] Input,
  input  in_2,
  output [11:0] out_3,
  output [11:0] out_4,
  output [11:0] Output,
  output [3:0] RS,
  output [3:0] RD,
  output [11:0] Result,
  output out_9
);

  wire alu_1_zero, and_1_out, clock_1_out, controlunit_1_ainv, controlunit_1_binv, controlunit_1_branch,
       controlunit_1_branch_sll, controlunit_1_cin, controlunit_1_dspen, controlunit_1_ensp,
       controlunit_1_input, controlunit_1_load, controlunit_1_memtoreg, controlunit_1_output,
       controlunit_1_rd_sp, controlunit_1_regwriteen, controlunit_1_store;
  wire [1:0] controlunit_1_rs_im_rd;
  wire [2:0] controlunit_1_aluop;
  wire [11:0] adder_1_out, adder_2_out, alu_1_result, bit_extender_1_out, multiplexer_1_out,
       multiplexer_2_out, multiplexer_3_out, multiplexer_6_out, ram_1_data, register_1_q, register_2_q,
       register_4_datard, register_4_datars, shifter_1_out, SP_q;
  wire [11:8] rom_1_data;

  Register_part #(.width(12)) register_1 (.D(multiplexer_6_out), .Q(register_1_q), .clk(clock_1_out));  // open: en, clr
  Clock clock_1 (.out(clock_1_out));
  Adder #(.width(12)) adder_1 (.a(12'h1), .b(register_1_q), .out(adder_1_out));  // open: cin, cout
  ControlUnit controlunit_1 (
    .in_1(rom_1_data), .EnSp(controlunit_1_ensp), .RegWriteEN(controlunit_1_regwriteen),
    .RS_Im_RD(controlunit_1_rs_im_rd), .RD_Sp(controlunit_1_rd_sp), .ALUOp(controlunit_1_aluop),
    .Cin(controlunit_1_cin), .Ainv(controlunit_1_ainv), .Binv(controlunit_1_binv),
    .MemToReg(controlunit_1_memtoreg), .Branch(controlunit_1_branch), .Load(controlunit_1_load),
    .Store(controlunit_1_store), .Branch_SLL(controlunit_1_branch_sll), .Input(controlunit_1_input),
    .Output(controlunit_1_output), .DspEn(controlunit_1_dspen));
  ROM #(.addrWidth(12), .dataWidth(12)) rom_1 (.addr(register_1_q), .data({rom_1_data, RD, RS}));  // open: sel
  Register_part #(.width(12)) register_2 (
    .D(Input), .en(controlunit_1_input), .Q(register_2_q), .clk(clock_1_out));  // open: clr
  Multiplexer #(.width(12), .enable("false")) multiplexer_1 (
    .in0(Result), .in1(register_2_q), .out(multiplexer_1_out), .sel(controlunit_1_input));
  Register_part #(.width(12)) SP (.D(Result), .en(controlunit_1_ensp), .Q(SP_q), .clk(clock_1_out));  // open: clr
  Register_part #(.width(12)) register_3 (
    .D(register_4_datard), .en(controlunit_1_output), .Q(Output), .clk(clock_1_out));  // open: clr
  assign bit_extender_1_out = {{8{1'b0}}, RS};  // Bit_Extender bit_extender_1
  Multiplexer #(.width(12), .enable("false")) multiplexer_2 (
    .in1(Output), .out(multiplexer_2_out), .sel(controlunit_1_dspen));  // open: in0
  Register register_4 (
    .RS(RS), .DataINPUT(multiplexer_1_out), .CLK(clock_1_out), .RD(RD), .RegWrite(controlunit_1_regwriteen),
    .DataRS(register_4_datars), .DataRD(register_4_datard));
  Multiplexer #(.width(12), .enable("false")) multiplexer_3 (
    .in0(bit_extender_1_out), .in1(SP_q), .out(multiplexer_3_out), .sel(controlunit_1_branch_sll));
  Multiplexer #(.width(12), .enable("false")) multiplexer_4 (
    .in0(register_4_datard), .in1(SP_q), .out(out_4), .sel(controlunit_1_rd_sp));
  Multiplexer #(.select(2), .width(12), .enable("false")) multiplexer_5 (
    .in0(register_4_datars), .in1(bit_extender_1_out), .in2(register_4_datard), .out(out_3),
    .sel(controlunit_1_rs_im_rd));  // open: in3
  Hex_Digit_Display hex_digit_display_1 (.value(multiplexer_2_out[11:8]));  // open: dp
  Hex_Digit_Display hex_digit_display_2 (.value(multiplexer_2_out[3:0]));  // open: dp
  Hex_Digit_Display hex_digit_display_3 (.value(multiplexer_2_out[7:4]));  // open: dp
  Shifter #(.width(12)) shifter_1 (.in(multiplexer_3_out), .\dist (4'b0010), .out(shifter_1_out));
  ALU alu_1 (
    .Cin(controlunit_1_cin), .Ainv(controlunit_1_ainv), .Binv(controlunit_1_binv),
    .Operation(controlunit_1_aluop), .Cout(out_9), .Result(alu_1_result), .Zero(alu_1_zero), .A(out_3),
    .B(out_4));
  Adder #(.width(12)) adder_2 (.a(adder_1_out), .b(shifter_1_out), .out(adder_2_out));  // open: cin, cout
  and and_1 (and_1_out, alu_1_zero, controlunit_1_branch);
  Multiplexer #(.width(12), .enable("false")) multiplexer_6 (
    .in0(adder_1_out), .in1(adder_2_out), .out(multiplexer_6_out), .sel(and_1_out));
  RAM #(.addrWidth(12), .dataWidth(12), .bus("separate")) ram_1 (
    .addr(alu_1_result), .din(register_4_datard), .data(ram_1_data), .str(controlunit_1_store),
    .clk(clock_1_out), .ld(controlunit_1_load), .clr(in_2));  // open: sel
  Multiplexer #(.width(12), .enable("false")) multiplexer_7 (
    .in0(ram_1_data), .in1(alu_1_result), .out(Result), .sel(controlunit_1_memtoreg));

  // Notes on the sheet:
  //   contents of rom_1 (hex, n*v repeats v):
  //   0 9c0
endmodule

module Register (
  input  [3:0] RS,
  input  [11:0] DataINPUT,
  input  CLK,
  input  [3:0] RD,
  input  RegWrite,
  output [11:0] DataRS,
  output [11:0] DataRD
);

  wire decoder_1_out0, decoder_1_out1, decoder_1_out2, decoder_1_out3, decoder_1_out4, decoder_1_out5,
       decoder_1_out6, decoder_1_out7, decoder_1_out8, decoder_1_out9, decoder_1_out10, decoder_1_out11,
       decoder_1_out12, decoder_1_out13, decoder_1_out14, decoder_1_out15;
  wire [11:0] register_1_q, register_2_q, register_3_q, register_4_q, register_5_q, register_6_q,
       register_7_q, register_8_q, register_9_q, register_10_q, register_11_q, register_12_q, register_13_q,
       register_14_q, register_15_q, register_16_q;

  Decoder #(.select(4)) decoder_1 (
    .out0(decoder_1_out0), .out1(decoder_1_out1), .out2(decoder_1_out2), .out3(decoder_1_out3),
    .out4(decoder_1_out4), .out5(decoder_1_out5), .out6(decoder_1_out6), .out7(decoder_1_out7),
    .out8(decoder_1_out8), .out9(decoder_1_out9), .out10(decoder_1_out10), .out11(decoder_1_out11),
    .out12(decoder_1_out12), .out13(decoder_1_out13), .out14(decoder_1_out14), .out15(decoder_1_out15),
    .sel(RD), .en(RegWrite));
  Register_part #(.width(12)) register_1 (
    .D(DataINPUT), .en(decoder_1_out0), .Q(register_1_q), .clk(CLK));  // open: clr
  Register_part #(.width(12)) register_2 (
    .D(DataINPUT), .en(decoder_1_out1), .Q(register_2_q), .clk(CLK));  // open: clr
  Register_part #(.width(12)) register_3 (
    .D(DataINPUT), .en(decoder_1_out2), .Q(register_3_q), .clk(CLK));  // open: clr
  Register_part #(.width(12)) register_4 (
    .D(DataINPUT), .en(decoder_1_out3), .Q(register_4_q), .clk(CLK));  // open: clr
  Register_part #(.width(12)) register_5 (
    .D(DataINPUT), .en(decoder_1_out4), .Q(register_5_q), .clk(CLK));  // open: clr
  Register_part #(.width(12)) register_6 (
    .D(DataINPUT), .en(decoder_1_out5), .Q(register_6_q), .clk(CLK));  // open: clr
  Register_part #(.width(12)) register_7 (
    .D(DataINPUT), .en(decoder_1_out6), .Q(register_7_q), .clk(CLK));  // open: clr
  Register_part #(.width(12)) register_8 (
    .D(DataINPUT), .en(decoder_1_out7), .Q(register_8_q), .clk(CLK));  // open: clr
  Register_part #(.width(12)) register_9 (
    .D(DataINPUT), .en(decoder_1_out8), .Q(register_9_q), .clk(CLK));  // open: clr
  Register_part #(.width(12)) register_10 (
    .D(DataINPUT), .en(decoder_1_out9), .Q(register_10_q), .clk(CLK));  // open: clr
  Register_part #(.width(12)) register_11 (
    .D(DataINPUT), .en(decoder_1_out10), .Q(register_11_q), .clk(CLK));  // open: clr
  Register_part #(.width(12)) register_12 (
    .D(DataINPUT), .en(decoder_1_out11), .Q(register_12_q), .clk(CLK));  // open: clr
  Register_part #(.width(12)) register_13 (
    .D(DataINPUT), .en(decoder_1_out12), .Q(register_13_q), .clk(CLK));  // open: clr
  Register_part #(.width(12)) register_14 (
    .D(DataINPUT), .en(decoder_1_out13), .Q(register_14_q), .clk(CLK));  // open: clr
  Register_part #(.width(12)) register_15 (
    .D(DataINPUT), .en(decoder_1_out14), .Q(register_15_q), .clk(CLK));  // open: clr
  Register_part #(.width(12)) register_16 (
    .D(DataINPUT), .en(decoder_1_out15), .Q(register_16_q), .clk(CLK));  // open: clr
  Multiplexer #(.select(4), .width(12), .enable("false")) multiplexer_1 (
    .in0(register_1_q), .in1(register_2_q), .in2(register_3_q), .in3(register_4_q), .in4(register_5_q),
    .in5(register_6_q), .in6(register_7_q), .in7(register_8_q), .in8(register_9_q), .in9(register_10_q),
    .in10(register_11_q), .in11(register_12_q), .in12(register_13_q), .in13(register_14_q),
    .in14(register_15_q), .in15(register_16_q), .out(DataRS), .sel(RS));
  Multiplexer #(.select(4), .width(12), .enable("false")) multiplexer_2 (
    .in0(register_1_q), .in1(register_2_q), .in2(register_3_q), .in3(register_4_q), .in4(register_5_q),
    .in5(register_6_q), .in6(register_7_q), .in7(register_8_q), .in8(register_9_q), .in9(register_10_q),
    .in10(register_11_q), .in11(register_12_q), .in12(register_13_q), .in13(register_14_q),
    .in14(register_15_q), .in15(register_16_q), .out(DataRD), .sel(RD));
endmodule

module ControlUnit (
  input  [3:0] in_1,
  output EnSp,
  output RegWriteEN,
  output [1:0] RS_Im_RD,
  output RD_Sp,
  output Branch_SLL,
  output [2:0] ALUOp,
  output Cin,
  output Ainv,
  output Binv,
  output MemToReg,
  output Branch,
  output Load,
  output Store,
  output Input,
  output Output,
  output DspEn
);

  wire add0000_out, addi0001_out, and0100_out, beq1011_out, jmp1101_out, otp1010_out, sll0011_out,
       slt1100_out, sub0010_out;

  and add0000 (add0000_out, ~in_1[3], ~in_1[2], ~in_1[1], ~in_1[0]);  // AND_Gate
  and addi0001 (addi0001_out, ~in_1[3], ~in_1[2], ~in_1[1], in_1[0]);  // AND_Gate
  and sub0010 (sub0010_out, ~in_1[3], ~in_1[2], in_1[1], ~in_1[0]);  // AND_Gate
  and sll0011 (sll0011_out, ~in_1[3], ~in_1[2], in_1[1], in_1[0]);  // AND_Gate
  and and0100 (and0100_out, ~in_1[3], in_1[2], ~in_1[1], ~in_1[0]);  // AND_Gate
  and nand0101 (Ainv, ~in_1[3], in_1[2], ~in_1[1], in_1[0]);  // AND_Gate
  and lw0110 (Load, ~in_1[3], in_1[2], in_1[1], ~in_1[0]);  // AND_Gate
  Register_part #(.width(12)) register_1 ();  // open: D, en, Q, clk, clr
  and sw0111 (Store, ~in_1[3], in_1[2], in_1[1], in_1[0]);  // AND_Gate
  and dsp1000 (DspEn, in_1[3], ~in_1[2], ~in_1[1], ~in_1[0]);  // AND_Gate
  and otp1010 (otp1010_out, in_1[3], ~in_1[2], in_1[1], ~in_1[0]);  // AND_Gate
  and inp1001 (Input, in_1[3], ~in_1[2], ~in_1[1], in_1[0]);  // AND_Gate
  and beq1011 (beq1011_out, in_1[3], ~in_1[2], in_1[1], in_1[0]);  // AND_Gate
  and slt1100 (slt1100_out, in_1[3], in_1[2], ~in_1[1], ~in_1[0]);  // AND_Gate
  and jmp1101 (jmp1101_out, in_1[3], in_1[2], ~in_1[1], in_1[0]);  // AND_Gate
  or or_1 (EnSp, sll0011_out, Load, Store, beq1011_out, slt1100_out);
  or or_2 (RegWriteEN, add0000_out, addi0001_out, sub0010_out, sll0011_out, and0100_out, Ainv, Load, Input);
  or or_3 (RS_Im_RD[0], addi0001_out, sll0011_out, Load, Store);
  or or_4 (RS_Im_RD[1], beq1011_out, jmp1101_out);
  or or_5 (RD_Sp, sll0011_out, Load, Store, beq1011_out, slt1100_out);
  or or_6 (Branch_SLL, sll0011_out, beq1011_out);
  or or_7 (ALUOp[0], sub0010_out, and0100_out, beq1011_out);
  or or_8 (ALUOp[1], sll0011_out, and0100_out, slt1100_out);
  or or_9 (ALUOp[2], Ainv, beq1011_out, slt1100_out);
  or or_10 (Cin, sub0010_out, beq1011_out);
  or or_11 (Binv, sub0010_out, Ainv, beq1011_out);
  or or_12 (MemToReg, add0000_out, addi0001_out, sub0010_out, sll0011_out, and0100_out, Ainv, Store);
  or or_13 (Branch, beq1011_out, jmp1101_out);
  or or_14 (Output, otp1010_out, DspEn);
endmodule

module ALU (
  input  [11:0] A,
  input  [11:0] B,
  input  Cin,
  input  Ainv,
  input  Binv,
  input  [2:0] Operation,
  output Cout,
  output [11:0] Result,
  output Zero
);

  wire comparator_1_lt, or_1_out;
  wire [3:0] bit_extender_1_out;
  wire [11:0] adder_1_out, and_1_out, bit_extender_2_out, multiplexer_1_out, multiplexer_2_out, nand_1_out,
       not_1_out, not_2_out, shifter_1_out;

  assign not_1_out = ~A;  // NOT_Gate not_1, 12 bits wide
  Multiplexer #(.width(12), .enable("false")) multiplexer_1 (
    .in0(A), .in1(not_1_out), .out(multiplexer_1_out), .sel(Ainv));
  Multiplexer #(.width(12), .enable("false")) multiplexer_2 (
    .in0(B), .in1(not_2_out), .out(multiplexer_2_out), .sel(Binv));
  assign not_2_out = ~B;  // NOT_Gate not_2, 12 bits wide
  Bit_Extender #(.in_width(12), .out_width(4)) bit_extender_1 (.in(multiplexer_2_out), .out(bit_extender_1_out));
  Adder #(.width(12)) adder_1 (.a(multiplexer_1_out), .b(multiplexer_2_out), .out(adder_1_out), .cin(Cin), .cout(Cout));
  Shifter #(.width(12)) shifter_1 (.in(multiplexer_1_out), .\dist (bit_extender_1_out), .out(shifter_1_out));
  assign and_1_out = multiplexer_1_out & multiplexer_2_out;  // AND_Gate and_1, 12 bits wide
  assign nand_1_out = ~(multiplexer_1_out & multiplexer_2_out);  // NAND_Gate nand_1, 12 bits wide
  Comparator #(.width(12), .mode("unsigned")) comparator_1 (
    .a(multiplexer_1_out), .b(multiplexer_2_out), .lt(comparator_1_lt));  // open: gt, eq
  assign bit_extender_2_out = {{11{1'b0}}, comparator_1_lt};  // Bit_Extender bit_extender_2
  Multiplexer #(.select(3), .width(12), .enable("false")) multiplexer_3 (
    .in0(adder_1_out), .in1(adder_1_out), .in2(shifter_1_out), .in3(and_1_out), .in4(nand_1_out),
    .in5(adder_1_out), .in6(bit_extender_2_out), .out(Result), .sel(Operation));  // open: in7
  or or_1 (or_1_out, Result[0], Result[1], Result[2], Result[3], Result[4], Result[5], Result[6], Result[7], Result[8], Result[9], Result[10], Result[11]);
  not not_3 (Zero, or_1_out);
endmodule
